# Fritzing sketch son hali (saved by Fritzing 1.0.6)

parts:
  Part1 = Arduino Mega 2560 (Rev3)
  M1 = DC Motor [voltage_(max)=24V voltage_(min)=12V]  # not connected
  BAT1 = 24 battery [package=battery]  # not connected
  M2 = RioRand LM2596
  J2 = Infrared Proximity Sensor  # not connected
  J3 = Infrared Proximity Sensor  # not connected
  M3 = DC Motor [voltage_(max)=24V voltage_(min)=12V]  # not connected
  M4 = DC Motor [voltage_(max)=24V voltage_(min)=12V]  # not connected
  M5 = DC Motor [voltage_(max)=24V voltage_(min)=12V]  # not connected
  J4 = Infrared Proximity Sensor  # not connected
  J5 = Infrared Proximity Sensor  # not connected
  J6 = Infrared Proximity Sensor  # not connected
  C1 = Electrolytic Capacitor [package="100 mil [THT, electrolytic]"]  # not connected

nets:
  N1: Part1.GND, M2.Pin_4
  N2: Part1.VIN, M2.Pin_3

notes:
  V+
  V-
  connect your power supply
  EN
  PWM
  MOTOR 1
  MOTOR 2
  MOTOR 3
  MOTOR 4
  24V -> 9V
  gnd
  vcc
  (-) hattı
  (-) hattı devamı
  (+) hattı

custom parts:
  24 battery: 24V lead acid type battery, like the Husqvarna YTH2448 12V 35AH battery. This is the mini version 1/4 the size of the actual battery to be closer to typical breadboard parts (around 2in wide rathher than 7in). The pads in pcb are sized to accomidate up to 14ga wire (as these batterys will deliver high currents.)
  Electrolytic Capacitor: A small electrolytic capacitor
